// Logisim project circ.circ as structural Verilog: 1 circuit, main circuit main
module main (
);

  wire CLK, d_ff_1_q;
  wire [6:0] xor_1_out;
  wire [7:0] adder_1_out, adder_2_out, multiplier_1_out, register_1_q, register_2_q, register_3_q,
       register_4_q, register_5_q, register_6_q, register_7_q, register_8_q, subtractor_1_out, undriven,
       undriven_2, undriven_3;

  Clock clock_1 (.out(CLK));
  Register register_1 (.D(undriven), .en(1'b1), .Q(register_1_q), .clk(CLK));  // open: clr
  Register register_2 (.D(undriven_2), .en(1'b1), .Q(register_2_q), .clk(CLK));  // open: clr
  Adder adder_1 (.a(register_1_q), .b(register_2_q), .out(adder_1_out));  // open: cin, cout
  Subtractor subtractor_1 (.a(register_1_q), .b(register_2_q), .out(subtractor_1_out));  // open: bin, bout
  Register register_3 (.D(adder_1_out), .en(1'b1), .Q(register_3_q), .clk(CLK));  // open: clr
  Register register_4 (.D(subtractor_1_out), .en(1'b1), .Q(register_4_q), .clk(CLK));  // open: clr
  Register register_5 (.D(undriven_3), .en(1'b1), .Q(register_5_q), .clk(CLK));  // open: clr
  Multiplier multiplier_1 (.a(register_3_q), .b(register_5_q), .out(multiplier_1_out));  // open: cin, cout
  xor xor_1 (xor_1_out[0], register_4_q[0], register_4_q[7]);
  xor xor_2 (xor_1_out[1], register_4_q[1], register_4_q[7]);
  xor xor_3 (xor_1_out[2], register_4_q[2], register_4_q[7]);
  xor xor_4 (xor_1_out[3], register_4_q[3], register_4_q[7]);
  xor xor_5 (xor_1_out[4], register_4_q[4], register_4_q[7]);
  xor xor_6 (xor_1_out[5], register_4_q[5], register_4_q[7]);
  xor xor_7 (xor_1_out[6], register_4_q[6], register_4_q[7]);
  D_Flip_Flop d_ff_1 (.D(register_4_q[7]), .Q(d_ff_1_q));  // open: clk, Qn, preset, en, reset
  Register register_6 (.D(multiplier_1_out), .en(1'b1), .Q(register_6_q), .clk(CLK));  // open: clr
  Register register_7 (.D({1'b0, xor_1_out}), .en(1'b1), .Q(register_7_q), .clk(CLK));  // open: clr
  Adder adder_2 (.a(register_6_q), .b(register_7_q), .out(adder_2_out), .cin(d_ff_1_q));  // open: cout
  Register register_8 (.D(adder_2_out), .en(1'b1), .Q(register_8_q), .clk(CLK));  // open: clr

  // Notes on the sheet:
  //   READ A
  //   READ B
  //   A + B
  //   A - B
  //   READ C
  //   (A + B) * C
  //   (A + B) * C + |A - B|
endmodule
